// Digital circuit ControlUnit.dig as structural Verilog
module ControlUnit (
  input  [7:0] FirstByte,
  input  [7:0] SecondByte,
  input  F_Greater,
  input  F_Less,
  input  F_Equal,
  input  F_NotEqual,
  input  Clock_5,
  input  Clock_4,
  input  Clock_3,
  input  Clock_2,
  input  Clock_1,
  input  Carry,
  input  Clock_6,
  input  Clock_7,
  input  Clock_8,
  output D_Clk_MDR,
  output D_Clk_SRAM,
  output D_Clk_RegOutput,
  output D_Clk_RegBufferSecond,
  output D_Clk_RegBufferFirst,
  output D_Clk_Flags,
  output D_Clk_RPC,
  output D_Clk_CIRSecond,
  output D_Clk_CIRFirst,
  output D_RPC_Registers,
  output D_RPC_MemAdder,
  output D_ALU_Increment,
  output S_CTL_Halt,
  output S_ADR_Direct,
  output S_ADR_Immediate,
  output S_ALU_OrOut,
  output S_ALU_ResultOut,
  output S_ALU_Propagate,
  output S_ALU_Invert,
  output S_ALU_CarryOut,
  output S_MEM_Store,
  output S_MDR_WriteMEM,
  output S_MDR_WriteALU,
  output S_REG_WriteMDR,
  output S_REG_WriteALU,
  output [3:0] Select,
  output [11:0] Value,
  output S_REG_WriteVAL
);

  wire signalintegrator_1_p15, signalintegrator_1_p16, signalintegrator_1_p18, signalintegrator_1_p20,
       signalintegrator_1_p22, signalintegrator_1_p25, signalintegrator_1_p27, signalintegrator_1_p31,
       signalintegrator_1_p32, signalintegrator_1_p33, staticcontrolunit_1_p4;
  wire [3:0] signalintegrator_1_p30, undriven, undriven_2;

  // StaticControlUnit staticcontrolunit_1: pin names not known; wires that end beside it: FirstByte, SecondByte, S_CTL_Halt, staticcontrolunit_1_p4, S_ADR_Direct, S_ADR_Immediate, S_ALU_OrOut, S_ALU_ResultOut, S_ALU_Propagate, S_ALU_Invert, S_ALU_CarryOut, S_MDR_WriteMEM, S_MDR_WriteALU, S_MEM_Store
  // SignalIntegrator signalintegrator_1: pin names not known; wires that end beside it: Clock_8, Clock_7, Clock_6, Clock_5, Clock_4, Clock_3, Clock_2, Clock_1, S_MDR_WriteMEM, S_MDR_WriteALU, S_MEM_Store, S_REG_WriteVAL, S_REG_WriteMDR, S_REG_WriteALU, signalintegrator_1_p15, signalintegrator_1_p16, F_NotEqual, signalintegrator_1_p18, F_Equal, signalintegrator_1_p20, F_Less, signalintegrator_1_p22, D_RPC_Registers, F_Greater, signalintegrator_1_p25, D_RPC_MemAdder, signalintegrator_1_p27, Carry, D_ALU_Increment, signalintegrator_1_p30, signalintegrator_1_p31, signalintegrator_1_p32, signalintegrator_1_p33
  OperandIntegrator operandintegrator_1 (
    .Nibble_4(signalintegrator_1_p30), .Nibble_3(undriven_2), .Nibble_2(undriven),
    .S_INS_ValRead(staticcontrolunit_1_p4), .D_CLK_SelectFirst(D_Clk_RegBufferFirst),
    .D_CLK_SelectSecond(D_Clk_RegBufferSecond), .Value(Value), .Select(Select));
endmodule
