// Digital circuit EEPROM.dig as structural Verilog
module EEPROM (
  input  [11:0] Address,
  output [7:0] Data
);

  SRAM sram_1 (
    .NC(1'b0), .A_0(Address[0]), .A_1(Address[1]), .A_2(Address[2]), .A_3(Address[3]), .A_4(Address[4]),
    .A_5(Address[5]), .A_6(Address[6]), .A_7(Address[7]), .A_8(Address[8]), .A_9(Address[9]),
    .A_10(Address[10]), .A_11(Address[11]), .OE(1'b0), .GND(1'b0), .VCC(1'b1), .WE(1'b1), .A_12(1'b0),
    .CS_2(1'b1), .CS_1(1'b0), .D_0(Data[0]), .D_1(Data[1]), .D_2(Data[2]), .D_3(Data[3]), .D_4(Data[4]),
    .D_5(Data[5]), .D_6(Data[6]), .D_7(Data[7]));
endmodule
