// Digital circuit SignalIntegrator.dig as structural Verilog
module SignalIntegrator (
  input  S_ALU_Increment,
  input  S_ALU_UseCarry,
  input  Clock_1,
  input  Clock_2,
  input  S_BRA_Branch,
  input  Clock_5,
  output D_ALU_Increment,
  output D_RPC_MemAdder,
  output D_RPC_Registers,
  output D_CLK_CIRFirst,
  output D_CLK_CIRSecond,
  output D_CLK_RPC
);

  wire not_1_out, or_1_out;

  or or_1 (or_1_out, Clock_1, Clock_2);
  xor xor_1 (D_ALU_Increment, S_ALU_Increment, S_ALU_UseCarry);
  and and_1 (D_RPC_MemAdder, or_1_out, not_1_out);
  not not_1 (not_1_out, S_BRA_Branch);
  and and_2 (D_RPC_Registers, S_BRA_Branch, Clock_5);

  assign D_CLK_CIRFirst = Clock_1;
  assign D_CLK_CIRSecond = Clock_2;
endmodule
